// Logisim project Components.circ as structural Verilog: 10 circuits, main circuit Instruction Decoder
module Data_Path (
  input  Clock,
  input  Reset,
  input  Instruction_Enable,
  input  Read_Write,
  input  ALU_Result_Enable,
  input  PC_Enable,
  input  in_7,
  input  [1:0] Adress_Selector,
  input  Value_Selector,
  input  [1:0] Branch_Selector,
  input  Selector_Extend,
  input  [3:0] ALU_Selector,
  input  [31:0] RAMData,
  input  [1:0] Selector_Destination_Adress,
  input  ALU_Selector_A,
  input  [2:0] Selector_Data,
  input  [1:0] ALU_Selector_B,
  input  [6:0] KBD_ASCII_Data,
  input  KBD_available,
  output [31:0] Adress,
  output [31:0] Value,
  output [6:0] TTY_DATA,
  output [5:0] Op_Code,
  output [5:0] Func_Code,
  output ZF,
  output NF,
  output EQF
);

  wire [4:0] multiplexer_2_out, Rd, Rs, Rt;
  wire [15:0] Constante;
  wire [25:0] Destino_Salto;
  wire [31:0] ALU, alu_1_out_6, bit_extender_1_out, bit_extender_2_out, bit_extender_3_out,
       branch_control_1_out_6, Data, Hi, KBD, Lo, multiplexer_4_out, multiplexer_5_out, multiplexer_6_out,
       multiplexer_7_out, PC, Random_Generator, register_1_q, RT_t, Sp;
  wire [31:7] RS_t;

  Random #(.width(32)) u_Random_Generator (.clk(Clock), .next(Clock), .out(Random_Generator));  // open: clr
  Register #(.width(32), .trigger("falling")) register_1 (
    .D(RAMData), .en(Instruction_Enable), .Q(register_1_q), .clk(Clock), .clr(Reset));
  Register #(.width(32)) register_2 (.D(RAMData), .en(Clock), .Q(Data), .clk(Clock), .clr(Reset));
  Branch_Control branch_control_1 (
    .in_1(PC), .in_2(Constante), .in_3(Destino_Salto), .in_4({RS_t, TTY_DATA}),
    .out_6(branch_control_1_out_6), .in_5(Branch_Selector));
  assign bit_extender_1_out = {{25{1'b0}}, KBD_ASCII_Data};  // Bit_Extender bit_extender_1
  Multiplexer #(.width(32), .enable("false")) multiplexer_1 (
    .in0({32{1'b1}}), .in1(bit_extender_1_out), .out(KBD), .sel(KBD_available));
  Instruction_Decoder instruction_decoder_1 (
    .in_1(register_1_q), .out_2(Op_Code), .out_3(Destino_Salto), .out_4(Rs), .out_5(Rt), .out_6(Constante),
    .out_7(Rd), .out_8(Func_Code));
  Program_Counter program_counter_1 (
    .in_1(branch_control_1_out_6), .PC_Enable(PC_Enable), .CLK(Clock), .Reset(Reset), .in_2(PC));
  Multiplexer #(.select(2), .width(5), .enable("false")) multiplexer_2 (
    .in0(Rd), .in1(Rt), .in2({5{1'b1}}), .out(multiplexer_2_out), .sel(Selector_Destination_Adress));  // open: in3
  assign bit_extender_2_out = {{16{Constante[15]}}, Constante};  // Bit_Extender bit_extender_2
  assign bit_extender_3_out = {{16{1'b0}}, Constante};  // Bit_Extender bit_extender_3
  Multiplexer #(.select(2), .width(32), .enable("false")) multiplexer_3 (
    .in0(PC), .in1(ALU), .in2(Sp), .out(Adress), .sel(Adress_Selector));  // open: in3
  Multiplexer #(.select(3), .width(32), .enable("false")) multiplexer_4 (
    .in0(ALU), .in1(Data), .in2(Hi), .in3(Lo), .in4(Random_Generator), .in5(KBD), .out(multiplexer_4_out),
    .sel(Selector_Data));  // open: in6, in7
  Multiplexer #(.width(32), .enable("false")) multiplexer_5 (
    .in0(bit_extender_2_out), .in1(bit_extender_3_out), .out(multiplexer_5_out), .sel(Selector_Extend));
  Multiplexer #(.select(2), .width(32), .enable("false")) multiplexer_6 (
    .in0(RT_t), .in1(32'h4), .in2(multiplexer_5_out), .out(multiplexer_6_out), .sel(ALU_Selector_B));  // open: in3
  Multiplexer #(.width(32), .enable("false")) multiplexer_7 (
    .in0({RS_t, TTY_DATA}), .in1(Sp), .out(multiplexer_7_out), .sel(ALU_Selector_A));
  Multiplexer #(.width(32), .enable("false")) multiplexer_8 (
    .in0({RS_t, TTY_DATA}), .in1(RT_t), .out(Value), .sel(Value_Selector));
  ALU alu_1 (
    .in_1(Clock), .in_2(ALU_Selector), .in_3(in_7), .in_4(multiplexer_7_out), .in_5(multiplexer_6_out),
    .out_6(alu_1_out_6), .out_9(Hi), .out_11(Lo), .out_7(ZF), .out_8(NF), .out_10(EQF));
  Register_File register_file_1 (
    .Data_Input(multiplexer_4_out), .Destination_Adress(multiplexer_2_out), .in_6(Rs), .in_7(Rt),
    .Output_A({RS_t, TTY_DATA}), .Output_B(RT_t), .SP(Sp), .Read_Write(Read_Write), .Clock(Clock),
    .Reset(Reset));
  Register #(.width(32)) register_3 (.D(alu_1_out_6), .en(ALU_Result_Enable), .Q(ALU), .clk(Clock), .clr(Reset));

  // Other names for the same wires on the sheet: ALU_Slc[3:0] = ALU_Selector; ALU_Slc_A = ALU_Selector_A;
  //   ALU_Slc_B[1:0] = ALU_Selector_B; Branch_Slc[1:0] = Branch_Selector; DA_Slc[1:0] = Selector_Destination_Adress;
  //   Data_Slc[2:0] = Selector_Data; Extend_Slc = Selector_Extend; Func[5:0] = Func_Code; HL_En = in_7;
  //   Op[5:0] = Op_Code; RS_t[6:0] = TTY_DATA

  // Notes on the sheet:
  //   Inputs
  //   DATA Path
  //   Output
endmodule

module Instruction_Decoder (
  input  [31:0] in_1,
  output [5:0] out_2,
  output [25:0] out_3,
  output [4:0] out_4,
  output [4:0] out_5,
  output [15:0] out_6,
  output [4:0] out_7,
  output [5:0] out_8
);


  assign out_2 = in_1[31:26];
  assign out_3 = in_1[25:0];
  assign out_4 = in_1[20:16];
  assign out_5 = in_1[25:21];
  assign out_6 = in_1[15:0];
  assign out_7 = in_1[15:11];
  assign out_8 = in_1[5:0];

  // Other names for the same wires on the sheet: Constante[15:0] = in_1[15:0]; Destino_Salto[25:0] = in_1[25:0];
  //   Func_Code[5:0] = in_1[5:0]; Rd[4:0] = in_1[15:11]; Rs[4:0] = in_1[20:16]; Rt[4:0] = in_1[25:21];
  //   Op_Code[5:0] = in_1[31:26]

  // Notes on the sheet:
  //   Instruction Decoder
  //   Outputs
endmodule

module Program_Counter (
  input  [31:0] in_1,
  input  [31:0] in_2,
  input  PC_Enable,
  input  CLK,
  input  Reset
);

  Register #(.width(32)) register_1 (.D(in_1), .en(PC_Enable), .Q(in_2), .clk(CLK), .clr(Reset));

  // Notes on the sheet:
  //   PC' (next instruction)
  //   Program Counter
  //   PC (current instruction)
endmodule

module Litte_Endian___Big_Endian (
  input  [31:0] in_1,
  output [31:0] out_2
);


  assign out_2 = {in_1[7:0], in_1[15:8], in_1[23:16], in_1[31:24]};

  // Notes on the sheet:
  //   Input
  //   Output
endmodule

module ALU (
  input  in_1,
  input  [3:0] in_2,
  input  in_3,
  input  [31:0] in_4,
  input  [31:0] in_5,
  output [31:0] out_6,
  output out_7,
  output out_8,
  output [31:0] out_9,
  output out_10,
  output [31:0] out_11
);

  wire comparator_1_lt;
  wire [1:0] Selector_Mult_Div;
  wire [31:0] ADD, AND, divider_1_out, divider_1_rem, multiplexer_1_out, multiplexer_2_out,
       multiplier_1_cout, NOR, OR, signed_divider_1_carry_out, signed_divider_1_result,
       signed_multiplier_1_out_3, signed_multiplier_1_out_4, SLT, SUB, XOR;

  assign AND = in_4 & in_5;  // AND_Gate and_1, 32 bits wide
  assign OR = in_4 | in_5;  // OR_Gate or_1, 32 bits wide
  assign NOR = ~(in_4 | in_5);  // NOR_Gate nor_1, 32 bits wide
  assign XOR = in_4 ^ in_5;  // XOR_Gate xor_1, 32 bits wide
  Signed_Multiplier signed_multiplier_1 (
    .in_1(in_4), .in_2(in_5), .out_3(signed_multiplier_1_out_3), .out_4(signed_multiplier_1_out_4));
  Multiplier #(.width(32)) multiplier_1 (
    .a(in_4), .b(in_5), .out(signed_multiplier_1_out_3), .cout(multiplier_1_cout));  // open: cin
  Signed_Divider signed_divider_1 (
    .in_1(in_4), .in_2(in_5), .Result(signed_divider_1_result), .Carry_Out(signed_divider_1_carry_out));
  Divider #(.width(32)) divider_1 (.a(in_4), .b(in_5), .out(divider_1_out), .rem(divider_1_rem));  // open: upper
  Adder #(.width(32)) adder_1 (.a(in_4), .b(in_5), .out(ADD));  // open: cin, cout
  Subtractor #(.width(32)) subtractor_1 (.a(in_4), .b(in_5), .out(SUB));  // open: bin, bout
  Comparator #(.width(32)) comparator_1 (.a(in_4), .b(in_5), .eq(out_10), .lt(comparator_1_lt));  // open: gt
  assign SLT = {{31{1'b0}}, comparator_1_lt};  // Bit_Extender bit_extender_1
  Multiplexer #(.select(2), .width(32), .enable("false")) multiplexer_1 (
    .in0(signed_multiplier_1_out_4), .in1(multiplier_1_cout), .in2(signed_divider_1_carry_out),
    .in3(divider_1_rem), .out(multiplexer_1_out), .sel(Selector_Mult_Div));
  Multiplexer #(.select(2), .width(32), .enable("false")) multiplexer_2 (
    .in0(signed_multiplier_1_out_3), .in1(signed_multiplier_1_out_3), .in2(signed_divider_1_result),
    .in3(divider_1_out), .out(multiplexer_2_out), .sel(Selector_Mult_Div));
  Register #(.width(32)) register_1 (.D(multiplexer_1_out), .en(in_3), .Q(out_9), .clk(in_1));  // open: clr
  Register #(.width(32)) register_2 (.D(multiplexer_2_out), .en(in_3), .Q(out_11), .clk(in_1));  // open: clr
  Multiplexer #(.select(4), .width(32), .enable("false")) multiplexer_3 (
    .in0(AND), .in1(OR), .in2(NOR), .in3(XOR), .in4(SLT), .in5(SLT), .in6(ADD), .in7(SUB), .out(out_6),
    .sel(in_2));  // open: in8, in9, in10, in11, in12, in13, in14, in15
  and and_2 (Selector_Mult_Div[0], in_2[3], ~in_2[2], in_2[0]);  // AND_Gate
  and and_3 (Selector_Mult_Div[1], in_2[1], ~in_2[2], in_2[3]);  // AND_Gate
  Comparator #(.width(32)) comparator_2 (.a(in_4), .b({32{1'b0}}), .eq(out_7), .lt(out_8));  // open: gt

  // Other names for the same wires on the sheet: A[31:0] = in_4; ALU_Selector[3:0] = in_2; B[31:0] = in_5; CLK = in_1;
  //   Enable_H_L = in_3; EQF = out_10; HIGH[31:0] = out_9; LOW[31:0] = out_11; NF = out_8; Output[31:0] = out_6;
  //   SLTU[31:0] = SLT; ZF = out_7

  // Notes on the sheet:
  //   Inputs
  //   Mult
  //   Div
  //   ALU
  //   (Restos)
  //   (Resultados)
  //   Outputs
endmodule

module Signed_Divider (
  input  [31:0] in_1,
  input  [31:0] in_2,
  output [31:0] Result,
  output [31:0] Carry_Out
);

  wire xor_1_out;
  wire [31:0] divider_1_out, multiplexer_1_out, multiplexer_2_out, negator_1_out, negator_2_out,
       negator_3_out;

  // Probe on in_1
  // Probe on in_2
  Negator #(.width(32)) negator_1 (.in(in_1), .out(negator_1_out));
  Negator #(.width(32)) negator_2 (.in(in_2), .out(negator_2_out));
  Multiplexer #(.width(32), .enable("false")) multiplexer_1 (
    .in0(in_1), .in1(negator_1_out), .out(multiplexer_1_out), .sel(in_1[31]));
  Multiplexer #(.width(32), .enable("false")) multiplexer_2 (
    .in0(in_2), .in1(negator_2_out), .out(multiplexer_2_out), .sel(in_2[31]));
  Divider #(.width(32)) divider_1 (
    .a(multiplexer_1_out), .b(multiplexer_2_out), .out(divider_1_out), .rem(Carry_Out));  // open: upper
  xor xor_1 (xor_1_out, in_1[31], in_2[31]);
  Negator #(.width(32)) negator_3 (.in(divider_1_out), .out(negator_3_out));
  // Probe on Carry_Out
  Multiplexer #(.width(32), .enable("false")) multiplexer_3 (
    .in0(divider_1_out), .in1(negator_3_out), .out(Result), .sel(xor_1_out));
  // Probe on Result

  // Notes on the sheet:
  //   A
  //   B
  //   Signed Divider
endmodule

module Signed_Multiplier (
  input  [31:0] in_1,
  input  [31:0] in_2,
  output [31:0] out_3,
  output [31:0] out_4
);

  wire adder_1_cout, xor_1_out;
  wire [31:0] adder_1_out, adder_2_out, multiplexer_1_out, multiplexer_2_out, multiplier_1_cout,
       multiplier_1_out, negator_1_out, negator_2_out, not_1_out, not_2_out;

  // Probe on in_1
  // Probe on in_2
  Negator #(.width(32)) negator_1 (.in(in_1), .out(negator_1_out));
  Negator #(.width(32)) negator_2 (.in(in_2), .out(negator_2_out));
  Multiplexer #(.width(32), .enable("false")) multiplexer_1 (
    .in0(in_1), .in1(negator_1_out), .out(multiplexer_1_out), .sel(in_1[31]));
  Multiplexer #(.width(32), .enable("false")) multiplexer_2 (
    .in0(in_2), .in1(negator_2_out), .out(multiplexer_2_out), .sel(in_2[31]));
  Multiplier #(.width(32)) multiplier_1 (
    .a(multiplexer_1_out), .b(multiplexer_2_out), .out(multiplier_1_out), .cout(multiplier_1_cout));  // open: cin
  xor xor_1 (xor_1_out, in_1[31], in_2[31]);
  // Probe on multiplier_1_out
  assign not_1_out = ~multiplier_1_out;  // NOT_Gate not_1, 32 bits wide
  assign not_2_out = ~multiplier_1_cout;  // NOT_Gate not_2, 32 bits wide
  Adder #(.width(32)) adder_1 (.a(not_1_out), .b(32'h1), .out(adder_1_out), .cout(adder_1_cout));  // open: cin
  Adder #(.width(32)) adder_2 (.a(not_2_out), .b({32{1'b0}}), .out(adder_2_out), .cin(adder_1_cout));  // open: cout
  Multiplexer #(.width(32), .enable("false")) multiplexer_3 (
    .in0(multiplier_1_out), .in1(adder_1_out), .out(out_3), .sel(xor_1_out));
  Multiplexer #(.width(32), .enable("false")) multiplexer_4 (
    .in0(multiplier_1_cout), .in1(adder_2_out), .out(out_4), .sel(xor_1_out));
  // Probe on out_3
  // Probe on out_4

  // Notes on the sheet:
  //   A
  //   B
  //   Signed Multiplier
endmodule

module Branch_Control (
  input  [31:0] in_1,
  input  [15:0] in_2,
  input  [25:0] in_3,
  input  [31:0] in_4,
  input  [1:0] in_5,
  output [31:0] out_6
);

  wire [15:0] multiplier_1_out;
  wire [31:0] bit_extender_1_out, PC__4, PC__4_Offset_4, Rs_t;

  Adder #(.width(32)) adder_1 (.a(in_1), .b(32'h4), .out(PC__4));  // open: cin, cout
  Multiplier #(.width(16)) multiplier_1 (.a(in_2), .b(16'h4), .out(multiplier_1_out));  // open: cin, cout
  assign bit_extender_1_out = {{16{multiplier_1_out[15]}}, multiplier_1_out};  // Bit_Extender bit_extender_1
  Adder #(.width(32)) adder_2 (.a(PC__4), .b(bit_extender_1_out), .out(PC__4_Offset_4));  // open: cin, cout
  Multiplexer #(.select(2), .width(32), .enable("false")) multiplexer_1 (
    .in0(PC__4), .in1(PC__4_Offset_4), .in2({in_1[31:28], in_3, 2'b00}), .in3(Rs_t), .out(out_6), .sel(in_5));

  // Other names for the same wires on the sheet: BS[1:0] = in_5; Destino[25:0] = in_3;
  //   Jump[31:2] = {in_1[31:28], in_3}; Offset[15:0] = in_2; PC[31:0] = in_1; PC_star[31:0] = out_6; RS[31:0] = in_4

  // Notes on the sheet:
  //   Inputs
  //   Branch Control
  //   Output
endmodule

module Register_File (
  input  Read_Write,
  input  Clock,
  input  Reset,
  input  [31:0] Data_Input,
  input  [4:0] Destination_Adress,
  input  [4:0] in_6,
  input  [4:0] in_7,
  output [31:0] Output_A,
  output [31:0] Output_B,
  output [31:0] SP
);

  wire Input_0, Input_1, Input_2, Input_3, Input_4, Input_5, Input_6, Input_7, Input_8, Input_9, Input_10,
       Input_11, Input_12, Input_13, Input_14, Input_15, Input_16, Input_17, Input_18, Input_19, Input_20,
       Input_21, Input_22, Input_23, Input_24, Input_25, Input_26, Input_27, Input_28, Input_29, Input_30,
       Input_31;
  wire [31:0] R0, R1, R2, R3, R4, R5, R6, R7, R8, R9, R10, R11, R12, R13, R14, R15, R16, R17, R18, R19, R20,
       R21, R22, R23, R24, R25, R26, R27, R28, R29, R30;

  Demultiplexer #(.select(5), .enable("false")) demultiplexer_1 (
    .out0(Input_0), .out1(Input_1), .out2(Input_2), .out3(Input_3), .out4(Input_4), .out5(Input_5),
    .out6(Input_6), .out7(Input_7), .out8(Input_8), .out9(Input_9), .out10(Input_10), .out11(Input_11),
    .out12(Input_12), .out13(Input_13), .out14(Input_14), .out15(Input_15), .out16(Input_16),
    .out17(Input_17), .out18(Input_18), .out19(Input_19), .out20(Input_20), .out21(Input_21),
    .out22(Input_22), .out23(Input_23), .out24(Input_24), .out25(Input_25), .out26(Input_26),
    .out27(Input_27), .out28(Input_28), .out29(Input_29), .out30(Input_30), .out31(Input_31),
    .in(Read_Write), .sel(Destination_Adress));
  Register #(.width(32)) u_R0 (.D({32{1'b0}}), .en(Input_0), .Q(R0), .clk(Clock), .clr(Reset));
  Register #(.width(32)) u_R1 (.D(Data_Input), .en(Input_1), .Q(R1), .clk(Clock), .clr(Reset));
  Register #(.width(32)) u_R2 (.D(Data_Input), .en(Input_2), .Q(R2), .clk(Clock), .clr(Reset));
  Register #(.width(32)) u_R3 (.D(Data_Input), .en(Input_3), .Q(R3), .clk(Clock), .clr(Reset));
  Register #(.width(32)) u_R4 (.D(Data_Input), .en(Input_4), .Q(R4), .clk(Clock), .clr(Reset));
  Register #(.width(32)) u_R5 (.D(Data_Input), .en(Input_5), .Q(R5), .clk(Clock), .clr(Reset));
  Register #(.width(32)) u_R6 (.D(Data_Input), .en(Input_6), .Q(R6), .clk(Clock), .clr(Reset));
  Register #(.width(32)) u_R7 (.D(Data_Input), .en(Input_7), .Q(R7), .clk(Clock), .clr(Reset));
  Register #(.width(32)) u_R8 (.D(Data_Input), .en(Input_8), .Q(R8), .clk(Clock), .clr(Reset));
  Register #(.width(32)) u_R9 (.D(Data_Input), .en(Input_9), .Q(R9), .clk(Clock), .clr(Reset));
  Register #(.width(32)) u_R10 (.D(Data_Input), .en(Input_10), .Q(R10), .clk(Clock), .clr(Reset));
  Register #(.width(32)) u_R11 (.D(Data_Input), .en(Input_11), .Q(R11), .clk(Clock), .clr(Reset));
  Register #(.width(32)) u_R12 (.D(Data_Input), .en(Input_12), .Q(R12), .clk(Clock), .clr(Reset));
  Register #(.width(32)) u_R13 (.D(Data_Input), .en(Input_13), .Q(R13), .clk(Clock), .clr(Reset));
  Register #(.width(32)) u_R14 (.D(Data_Input), .en(Input_14), .Q(R14), .clk(Clock), .clr(Reset));
  Register #(.width(32)) u_R15 (.D(Data_Input), .en(Input_15), .Q(R15), .clk(Clock), .clr(Reset));
  Register #(.width(32)) u_R16 (.D(Data_Input), .en(Input_16), .Q(R16), .clk(Clock), .clr(Reset));
  Register #(.width(32)) u_R17 (.D(Data_Input), .en(Input_17), .Q(R17), .clk(Clock), .clr(Reset));
  Register #(.width(32)) u_R18 (.D(Data_Input), .en(Input_18), .Q(R18), .clk(Clock), .clr(Reset));
  Register #(.width(32)) u_R19 (.D(Data_Input), .en(Input_19), .Q(R19), .clk(Clock), .clr(Reset));
  Register #(.width(32)) u_R20 (.D(Data_Input), .en(Input_20), .Q(R20), .clk(Clock), .clr(Reset));
  Register #(.width(32)) u_R21 (.D(Data_Input), .en(Input_21), .Q(R21), .clk(Clock), .clr(Reset));
  Register #(.width(32)) u_R22 (.D(Data_Input), .en(Input_22), .Q(R22), .clk(Clock), .clr(Reset));
  Register #(.width(32)) u_R23 (.D(Data_Input), .en(Input_23), .Q(R23), .clk(Clock), .clr(Reset));
  Register #(.width(32)) u_R24 (.D(Data_Input), .en(Input_24), .Q(R24), .clk(Clock), .clr(Reset));
  Multiplexer #(.select(5), .width(32), .enable("false")) multiplexer_1 (
    .in0(R0), .in1(R1), .in2(R2), .in3(R3), .in4(R4), .in5(R5), .in6(R6), .in7(R7), .in8(R8), .in9(R9),
    .in10(R10), .in11(R11), .in12(R12), .in13(R13), .in14(R14), .in15(R15), .in16(R16), .in17(R17),
    .in18(R18), .in19(R19), .in20(R20), .in21(R21), .in22(R22), .in23(R23), .in24(R24), .in25(R25),
    .in26(R26), .in27(R27), .in28(R28), .in29(R29), .in30(R30), .in31(SP), .out(Output_A), .sel(in_6));
  Register #(.width(32)) u_R25 (.D(Data_Input), .en(Input_25), .Q(R25), .clk(Clock), .clr(Reset));
  Register #(.width(32)) u_R26 (.D(Data_Input), .en(Input_26), .Q(R26), .clk(Clock), .clr(Reset));
  Register #(.width(32)) u_R27 (.D(Data_Input), .en(Input_27), .Q(R27), .clk(Clock), .clr(Reset));
  Register #(.width(32)) u_R28 (.D(Data_Input), .en(Input_28), .Q(R28), .clk(Clock), .clr(Reset));
  Register #(.width(32)) u_R29 (.D(Data_Input), .en(Input_29), .Q(R29), .clk(Clock), .clr(Reset));
  Register #(.width(32)) u_R30 (.D(Data_Input), .en(Input_30), .Q(R30), .clk(Clock), .clr(Reset));
  Register #(.width(32)) u_SP (.D(Data_Input), .en(Input_31), .Q(SP), .clk(Clock), .clr(Reset));
  Multiplexer #(.select(5), .width(32), .enable("false")) multiplexer_2 (
    .in0(R0), .in1(R1), .in2(R2), .in3(R3), .in4(R4), .in5(R5), .in6(R6), .in7(R7), .in8(R8), .in9(R9),
    .in10(R10), .in11(R11), .in12(R12), .in13(R13), .in14(R14), .in15(R15), .in16(R16), .in17(R17),
    .in18(R18), .in19(R19), .in20(R20), .in21(R21), .in22(R22), .in23(R23), .in24(R24), .in25(R25),
    .in26(R26), .in27(R27), .in28(R28), .in29(R29), .in30(R30), .in31(SP), .out(Output_B), .sel(in_7));

  // Other names for the same wires on the sheet: Data[31:0] = Data_Input; Destination[4:0] = Destination_Adress;
  //   R31[31:0] = SP; ReadWrite = Read_Write; Selector_A[4:0] = in_6; Selector_B[4:0] = in_7

  // Notes on the sheet:
  //   Inputs
  //   Register File
  //   Outputs
endmodule

module Cache (
  input  [31:0] in_1,
  input  [31:0] in_2,
  input  [31:0] in_3,
  input  in_4,
  input  in_5,
  input  in_6,
  input  [31:0] in_7,
  input  [31:0] in_8,
  output out_9,
  output [31:0] out_10
);

  wire Col_00, Col_01, Col_02, Col_03, Col_10, Col_11, Col_12, Col_13, Col_20, Col_21, Col_22, Col_23,
       Col_30, Col_31, Col_32, Col_33, Col_40, Col_41, Col_42, Col_43, Col_50, Col_51, Col_52, Col_53,
       Col_60, Col_61, Col_62, Col_63, Col_70, Col_71, Col_72, Col_73, comparator_1_eq, Idex_0, Idex_1,
       Idex_2, Idex_3, Idex_4, Idex_5, Idex_6, Idex_7, V, V0, V1, V2, V3, V4, V5, V7, V8;
  wire [3:0] _6n_Index6, En_Index0, En_Index1, En_Index2, En_Index3, En_Index4, En_Index5, En_Index6,
       En_Index7, En_Offset;
  wire [26:0] T0, T1, T2, T3, T4, T5, T6, T7, Tag_star;
  wire [31:0] multiplexer_5_out, Out0, Out1, Out2, Out3, R00, R01, R02, R03, R10, R11, R12, R13, R20, R21,
       R22, R23, R30, R31, R32, R33, R40, R41, R42, R43, R50, R51, R52, R53, R60, R61, R62, R63, R70, R71,
       R72, R73;

  Register #(.width(1)) R0 (.D(1'b1), .en(Idex_0), .Q(V0), .clk(in_4), .clr(in_5));
  Register #(.width(1)) R1 (.D(1'b1), .en(Idex_1), .Q(V1), .clk(in_4), .clr(in_5));
  Register #(.width(1)) R2 (.D(1'b1), .en(Idex_2), .Q(V2), .clk(in_4), .clr(in_5));
  Register #(.width(1)) R3 (.D(1'b1), .en(Idex_3), .Q(V3), .clk(in_4), .clr(in_5));
  Register #(.width(1)) R4 (.D(1'b1), .en(Idex_4), .Q(V4), .clk(in_4), .clr(in_5));
  Register #(.width(1)) R2_2 (.D(1'b1), .en(Idex_5), .Q(V5), .clk(in_4), .clr(in_5));
  Register #(.width(1)) R3_2 (.D(1'b1), .en(Idex_6), .Q(V7), .clk(in_4), .clr(in_5));
  Register #(.width(1)) R4_2 (.D(1'b1), .en(Idex_7), .Q(V8), .clk(in_4), .clr(in_5));
  Multiplexer #(.select(3), .width(32), .enable("false")) multiplexer_1 (
    .in0(R00), .in1(R10), .in2(R20), .in3(R30), .in4(R40), .in5(R50), .in6(R60), .in7(R70), .out(Out0),
    .sel({in_1[7], in_1[1:0]}));
  Register #(.width(27)) R5 (.D({in_1[31:8], in_1[6:4]}), .en(Idex_0), .Q(T0), .clk(in_4), .clr(in_5));
  Register #(.width(27)) R6 (.D({in_1[31:8], in_1[6:4]}), .en(Idex_1), .Q(T1), .clk(in_4), .clr(in_5));
  Register #(.width(27)) R7 (.D({in_1[31:8], in_1[6:4]}), .en(Idex_2), .Q(T2), .clk(in_4), .clr(in_5));
  Register #(.width(27)) R8 (.D({in_1[31:8], in_1[6:4]}), .en(Idex_3), .Q(T3), .clk(in_4), .clr(in_5));
  Register #(.width(27)) R9 (.D({in_1[31:8], in_1[6:4]}), .en(Idex_4), .Q(T4), .clk(in_4), .clr(in_5));
  Register #(.width(27)) R7_2 (.D({in_1[31:8], in_1[6:4]}), .en(Idex_5), .Q(T5), .clk(in_4), .clr(in_5));
  Register #(.width(27)) R8_2 (.D({in_1[31:8], in_1[6:4]}), .en(Idex_6), .Q(T6), .clk(in_4), .clr(in_5));
  Register #(.width(27)) R9_2 (.D({in_1[31:8], in_1[6:4]}), .en(Idex_7), .Q(T7), .clk(in_4), .clr(in_5));
  Multiplexer #(.select(3), .width(32), .enable("false")) multiplexer_2 (
    .in0(R01), .in1(R11), .in2(R21), .in3(R31), .in4(R41), .in5(R51), .in6(R61), .in7(R71), .out(Out1),
    .sel({in_1[7], in_1[1:0]}));
  Register #(.width(32)) u_R10 (.D(in_2), .en(Col_00), .Q(R00), .clk(in_4), .clr(in_5));
  Register #(.width(32)) u_R11 (.D(in_2), .en(Col_10), .Q(R10), .clk(in_4), .clr(in_5));
  Register #(.width(32)) u_R12 (.D(in_2), .en(Col_20), .Q(R20), .clk(in_4), .clr(in_5));
  Register #(.width(32)) u_R13 (.D(in_2), .en(Col_30), .Q(R30), .clk(in_4), .clr(in_5));
  Register #(.width(32)) R14 (.D(in_2), .en(Col_40), .Q(R40), .clk(in_4), .clr(in_5));
  Register #(.width(32)) R12_2 (.D(in_2), .en(Col_50), .Q(R50), .clk(in_4), .clr(in_5));
  Register #(.width(32)) R13_2 (.D(in_2), .en(Col_60), .Q(R60), .clk(in_4), .clr(in_5));
  Register #(.width(32)) R14_2 (.D(in_2), .en(Col_70), .Q(R70), .clk(in_4), .clr(in_5));
  Multiplexer #(.select(3), .width(32), .enable("false")) multiplexer_3 (
    .in0(R02), .in1(R12), .in2(R22), .in3(R32), .in4(R42), .in5(R52), .in6(R62), .in7(R72), .out(Out2),
    .sel({in_1[7], in_1[1:0]}));
  Register #(.width(32)) R15 (.D(in_3), .en(Col_01), .Q(R01), .clk(in_4), .clr(in_5));
  Register #(.width(32)) R16 (.D(in_3), .en(Col_11), .Q(R11), .clk(in_4), .clr(in_5));
  Register #(.width(32)) R17 (.D(in_3), .en(Col_21), .Q(R21), .clk(in_4), .clr(in_5));
  Register #(.width(32)) R18 (.D(in_3), .en(Col_31), .Q(R31), .clk(in_4), .clr(in_5));
  Register #(.width(32)) R19 (.D(in_3), .en(Col_41), .Q(R41), .clk(in_4), .clr(in_5));
  Register #(.width(32)) R17_2 (.D(in_3), .en(Col_51), .Q(R51), .clk(in_4), .clr(in_5));
  Register #(.width(32)) R18_2 (.D(in_3), .en(Col_61), .Q(R61), .clk(in_4), .clr(in_5));
  Register #(.width(32)) R19_2 (.D(in_3), .en(Col_71), .Q(R71), .clk(in_4), .clr(in_5));
  Multiplexer #(.select(3), .width(32), .enable("false")) multiplexer_4 (
    .in0(R03), .in1(R13), .in2(R23), .in3(R33), .in4(R43), .in5(R53), .in6(R63), .in7(R73), .out(Out3),
    .sel({in_1[7], in_1[1:0]}));
  Comparator #(.width(27)) comparator_1 (
    .a(Tag_star), .b({in_1[31:8], in_1[6:4]}), .eq(comparator_1_eq));  // open: gt, lt
  Register #(.width(32)) u_R20 (.D(in_7), .en(Col_02), .Q(R02), .clk(in_4), .clr(in_5));
  Register #(.width(32)) u_R21 (.D(in_7), .en(Col_12), .Q(R12), .clk(in_4), .clr(in_5));
  Register #(.width(32)) u_R22 (.D(in_7), .en(Col_22), .Q(R22), .clk(in_4), .clr(in_5));
  Register #(.width(32)) u_R23 (.D(in_7), .en(Col_32), .Q(R32), .clk(in_4), .clr(in_5));
  Register #(.width(32)) R24 (.D(in_7), .en(Col_42), .Q(R42), .clk(in_4), .clr(in_5));
  Register #(.width(32)) R22_2 (.D(in_7), .en(Col_52), .Q(R52), .clk(in_4), .clr(in_5));
  Register #(.width(32)) R23_2 (.D(in_7), .en(Col_62), .Q(R62), .clk(in_4), .clr(in_5));
  Register #(.width(32)) R24_2 (.D(in_7), .en(Col_72), .Q(R72), .clk(in_4), .clr(in_5));
  and and_1 (out_9, comparator_1_eq, V);
  Multiplexer #(.select(2), .width(32), .enable("false")) multiplexer_5 (
    .in0(Out0), .in1(Out1), .in2(Out2), .in3(Out3), .out(multiplexer_5_out), .sel(in_1[3:2]));
  Register #(.width(32)) R25 (.D(in_8), .en(Col_03), .Q(R03), .clk(in_4), .clr(in_5));
  Register #(.width(32)) R26 (.D(in_8), .en(Col_13), .Q(R13), .clk(in_4), .clr(in_5));
  Register #(.width(32)) R27 (.D(in_8), .en(Col_23), .Q(R23), .clk(in_4), .clr(in_5));
  Register #(.width(32)) R28 (.D(in_8), .en(Col_33), .Q(R33), .clk(in_4), .clr(in_5));
  Register #(.width(32)) R29 (.D(in_8), .en(Col_43), .Q(R43), .clk(in_4), .clr(in_5));
  Register #(.width(32)) R27_2 (.D(in_8), .en(Col_53), .Q(R53), .clk(in_4), .clr(in_5));
  Register #(.width(32)) R28_2 (.D(in_8), .en(Col_63), .Q(R63), .clk(in_4), .clr(in_5));
  Register #(.width(32)) R29_2 (.D(in_8), .en(Col_73), .Q(R73), .clk(in_4), .clr(in_5));
  Litte_Endian___Big_Endian litte_endian_big_endian_1 (.in_1(multiplexer_5_out), .out_2(out_10));
  Decoder #(.select(2), .enable("false")) decoder_1 (
    .out0(En_Offset[0]), .out1(En_Offset[1]), .out2(En_Offset[2]), .out3(En_Offset[3]), .sel(in_1[3:2]));
  Demultiplexer #(.select(3), .enable("false")) demultiplexer_1 (
    .out0(Idex_0), .out1(Idex_1), .out2(Idex_2), .out3(Idex_3), .out4(Idex_4), .out5(Idex_5), .out6(Idex_6),
    .out7(Idex_7), .in(in_6), .sel({in_1[7], in_1[1:0]}));
  Multiplexer #(.select(3), .width(27), .enable("false")) multiplexer_6 (
    .in0(T0), .in1(T1), .in2(T2), .in3(T3), .in4(T4), .in5(T5), .in6(T6), .in7(T7), .out(Tag_star),
    .sel({in_1[7], in_1[1:0]}));
  Multiplexer #(.select(3), .enable("false")) multiplexer_7 (
    .in0(V0), .in1(V1), .in2(V2), .in3(V3), .in4(V4), .in5(V5), .in6(V7), .in7(V8), .out(V),
    .sel({in_1[7], in_1[1:0]}));
  Bit_Extender #(.in_width(1), .out_width(4), .\type ("input")) bit_extender_1 (
    .in(Idex_0), .extend(Idex_0));  // open: out
  assign En_Index1 = {{3{Idex_1}}, Idex_1};  // Bit_Extender bit_extender_2
  assign En_Index2 = {{3{Idex_2}}, Idex_2};  // Bit_Extender bit_extender_3
  assign En_Index3 = {{3{Idex_3}}, Idex_3};  // Bit_Extender bit_extender_4
  assign {Col_03, Col_02, Col_01, Col_00} = En_Offset & En_Index0;  // AND_Gate and_2, 4 bits wide
  assign {Col_13, Col_12, Col_11, Col_10} = En_Offset & En_Index1;  // AND_Gate and_3, 4 bits wide
  assign {Col_23, Col_22, Col_21, Col_20} = En_Offset & En_Index2;  // AND_Gate and_4, 4 bits wide
  assign {Col_33, Col_32, Col_31, Col_30} = En_Offset & En_Index3;  // AND_Gate and_5, 4 bits wide
  assign En_Index4 = {{3{Idex_4}}, Idex_4};  // Bit_Extender bit_extender_5
  assign En_Index5 = {{3{Idex_5}}, Idex_5};  // Bit_Extender bit_extender_6
  assign _6n_Index6 = {{3{Idex_6}}, Idex_6};  // Bit_Extender bit_extender_7
  assign En_Index7 = {{3{Idex_7}}, Idex_7};  // Bit_Extender bit_extender_8
  assign {Col_43, Col_42, Col_41, Col_40} = En_Offset & En_Index4;  // AND_Gate and_6, 4 bits wide
  assign {Col_53, Col_52, Col_51, Col_50} = En_Offset & En_Index5;  // AND_Gate and_7, 4 bits wide
  assign {Col_63, Col_62, Col_61, Col_60} = En_Offset & En_Index6;  // AND_Gate and_8, 4 bits wide
  assign {Col_73, Col_72, Col_71, Col_70} = En_Offset & En_Index7;  // AND_Gate and_9, 4 bits wide

  // Other names for the same wires on the sheet: Block0[31:0] = in_2; Block1[31:0] = in_3; Block2[31:0] = in_7;
  //   Block3[31:0] = in_8; Clock = in_4; Data[31:0] = out_10; HIT = out_9; Index[2:0] = {in_1[7], in_1[1:0]};
  //   Offset[1:0] = in_1[3:2]; Tag[26:0] = {in_1[31:8], in_1[6:4]}; ReadWrite = in_6; Reset = in_5

  // Notes on the sheet:
  //   in_6: pull=down
  //   Validate
  //   Instruction
  //   Inputs
  //   Block 0
  //   Block 2
  //   Tag
  //   Block 1
  //   Block 3
  //   Outputs
  //   Offset
endmodule
